// Logisim project corg-final.circ as structural Verilog: 2 circuits, main circuit main
module main (
  output [15:0] out_1
);

  wire clock_1_out, IR_EN, IR_LH, MEM_CLR, MEM_LD, MEM_SEL, MEM_STR, MuxCSel;
  wire [1:0] _3RB_FS, _4RB_FS, IR_FS, MuxASel, MuxBSel, OutASel, OutBSel, OutCSel, OutDSel;
  wire [2:0] F1, F2;
  wire [3:0] _3RB_RS, _4RB_RS, ALUFlags, ALUFS;

  Clock clock_1 (.out(clock_1_out));
  CONTROL_UNIT control_unit_1 (
    .in_2(out_1[8]), .NEGATIVE_FLAG(ALUFlags[2]), .ZERO_FLAG(ALUFlags[3]), .OPCODE(out_1[15:11]), .out_6(F1),
    .out_7(F2), .in_1(clock_1_out));
  part2_edited_main main_1 (
    .OutASel(OutASel), .OutBSel(OutBSel), .FunSel_2(_4RB_FS), .RegSel(_4RB_RS), .MuxASel(MuxASel),
    .OutCSel(OutCSel), .OutDSel(OutDSel), .FunSel_3(_3RB_FS), .RegSel_2(_3RB_RS), .L_H(IR_LH),
    .Enable(IR_EN), .FunSel_4(IR_FS), .MuxCSel(MuxCSel), .MuxBSel(MuxBSel), .FunSel(ALUFS), .in_10(MEM_STR),
    .in_11(MEM_SEL), .in_12(MEM_LD), .in_13(MEM_CLR), .out_22(ALUFlags), .out_23(out_1), .in_2(clock_1_out));  // open: out_21
  Hex_Digit_Display hex_digit_display_1 (.value(out_1[15:12]));  // open: dp
  Hex_Digit_Display hex_digit_display_2 (.value(out_1[11:8]));  // open: dp
  Hex_Digit_Display hex_digit_display_3 (.value(out_1[7:4]));  // open: dp
  Hex_Digit_Display hex_digit_display_4 (.value(out_1[3:0]));  // open: dp

  // Other names for the same wires on the sheet: ADDRESS[7:0] = out_1[7:0]; INSTR[15:0] = out_1;
  //   SRCREG2[2:0] = out_1[4:2]; SRCREG1[2:0] = out_1[7:5]; AdrMOD = out_1[8]; DESTREG[2:0] = out_1[10:8];
  //   REGSEL[1:0] = out_1[10:9]; OPCODE[4:0] = out_1[15:11]
endmodule

module CONTROL_UNIT (
  input  in_1,
  input  in_2,
  input  NEGATIVE_FLAG,
  input  ZERO_FLAG,
  input  [4:0] OPCODE,
  output [2:0] out_6,
  output [2:0] out_7
);

  wire and_1_out, and_2_out, and_3_out, and_4_out, decoder_1_out0, decoder_1_out1, decoder_1_out2,
       decoder_1_out3, multiplexer_1_out, not_1_out, not_2_out;
  wire [1:0] rom_1_data_4, rom_1_data_5;
  wire [2:0] rom_1_data, rom_1_data_2;
  wire [7:0] adder_1_out, controlled_buffer_1_out, controlled_buffer_4_out, register_1_q, register_2_q,
       rom_1_data_3;
  wire [7:2] adder_2_out;

  not not_1 (not_1_out, multiplexer_1_out);
  and and_1 (and_1_out, decoder_1_out0, not_1_out);
  Adder adder_1 (.a(register_1_q), .b(8'h1), .out(adder_1_out));  // open: cin, cout
  assign controlled_buffer_1_out = and_1_out ? adder_1_out : 8'bz;  // Controlled_Buffer controlled_buffer_1
  and and_2 (and_2_out, decoder_1_out0, multiplexer_1_out);
  assign controlled_buffer_1_out = and_2_out ? rom_1_data_3 : 8'bz;  // Controlled_Buffer controlled_buffer_2
  and and_3 (and_3_out, decoder_1_out1, multiplexer_1_out);
  assign controlled_buffer_1_out = and_3_out ? rom_1_data_3 : 8'bz;  // Controlled_Buffer controlled_buffer_3
  assign controlled_buffer_4_out = and_3_out ? adder_1_out : 8'bz;  // Controlled_Buffer controlled_buffer_4
  not not_2 (not_2_out, multiplexer_1_out);
  and and_4 (and_4_out, decoder_1_out1, not_2_out);
  assign controlled_buffer_1_out = and_4_out ? adder_1_out : 8'bz;  // Controlled_Buffer controlled_buffer_5
  Register register_1 (.D(controlled_buffer_1_out), .Q(register_1_q), .clk(in_1));  // open: en, clr
  Register register_2 (.D(controlled_buffer_4_out), .en(and_3_out), .Q(register_2_q), .clk(in_1));  // open: clr
  assign controlled_buffer_1_out = decoder_1_out2 ? register_2_q : 8'bz;  // Controlled_Buffer controlled_buffer_6
  Decoder #(.select(2), .enable("false")) decoder_1 (
    .out0(decoder_1_out0), .out1(decoder_1_out1), .out2(decoder_1_out2), .out3(decoder_1_out3),
    .sel(rom_1_data_4));
  assign controlled_buffer_1_out = decoder_1_out3 ? {adder_2_out, 2'b00} : 8'bz;  // Controlled_Buffer controlled_buffer_7
  ROM #(.dataWidth(24)) rom_1 (
    .addr(register_1_q),
    .data({out_7, out_6, rom_1_data_5, rom_1_data_4, rom_1_data_3, rom_1_data_2, rom_1_data}));  // open: sel
  Multiplexer #(.select(2), .enable("false")) multiplexer_1 (
    .in0(1'b1), .in1(in_2), .in2(NEGATIVE_FLAG), .in3(ZERO_FLAG), .out(multiplexer_1_out), .sel(rom_1_data_5));
  Adder #(.width(5)) adder_2 (.a(OPCODE), .b(5'b00001), .out(adder_2_out[6:2]), .cout(adder_2_out[7]));  // open: cin

  // Notes on the sheet:
  //   CAR
  //   SP
  //   Control Unit
  //   Control Memory
  //   contents of rom_1 (hex, n*v repeats v):
  //   4200 0 0 8000 4*0 14200 10600 600 13*0 8000
  //   IR LOW PLACEHOLDER
endmodule
